# Fritzing sketch ExamenBreadboardBeforeSoldering (saved by Fritzing 0.9.9b)
breadboards: 1

parts:
  VCC1 = Battery  # not connected
  R1 = Resistor [tolerance=±5% power=0.25 resistance=220 package=THT]  # not connected
  S1 = Pushbutton [package="[THT]"]
  Компонент1 = Passive Buzzer  # not connected

nets:
  N1: S1.Pin_1, S1.Pin_2
  N2: S1.Pin_3, S1.Pin_4
