# Fritzing sketch programmator-esp32-cam (saved by Fritzing 1.0.2b)
breadboards: 1

parts:
  ESP32-CAM1 = ESP32-CAM_tve
  R1 = Resistor [tolerance=±5% power=0.25W resistance=10k package=THT]
  battery1 = Battery3AAA [part_number=001 package=Pack-tve]
  S3 = Square Pushbutton
  S4 = Momentary Switch [package=ksa_sealed_tac_switch]
  USB_UART1 = USB-TTL UART

nets:
  N1: ESP32-CAM1.GND#7, battery1.-, S4.4, USB_UART1.pin6
  N2: ESP32-CAM1.5V, R1.Pin_1, battery1.+, USB_UART1.pin7
  N3: ESP32-CAM1.GPIO0, S3.leg0
  N4: ESP32-CAM1.GND#12, S3.leg1
  N5: ESP32-CAM1.GPIO3_/_RX, USB_UART1.pin8
  N6: ESP32-CAM1.GPIO1_/_TX, USB_UART1.pin9
  N7: ESP32-CAM1.GND#16, R1.Pin_0, S4.2

custom parts:
  ESP32-CAM_tve: The ESP32-CAM has a very competitive small-size camera module that can operate independently as a minimum system with a footprint of only 27*40.5*4.5mm and a deep sleep current of up to 6mA.
  Battery3AAA: Блок 3 элементов питания AAA по 1.5В
  USB-TTL UART: USB programmer interface incorporating Silicon Labs CP2102 UART
