# Fritzing sketch podklyuchenie-esp32-cam-k-programmatoru (saved by Fritzing 1.0.2b)
breadboards: 1

parts:
  battery1 = Battery3AAA [part_number=001 package=Pack-tve]
  ESP32_-_Front1 = ESP32 - CAM
  FTDI_USB_UART1 = CP2102 USB UART [part_number="USB UART"]

nets:
  N1: battery1.-, ESP32_-_Front1.GND#7
  N2: battery1.+, ESP32_-_Front1.5V
  N3: ESP32_-_Front1.GPIO0, ESP32_-_Front1.GND#12
  N4: ESP32_-_Front1.GPIO3_/_RX, FTDI_USB_UART1.TXO
  N5: ESP32_-_Front1.GPIO1_/_TX, FTDI_USB_UART1.RXI
  N6: ESP32_-_Front1.GND#16, FTDI_USB_UART1.GND

custom parts:
  Battery3AAA: Блок 3 элементов питания AAA по 1.5В
  ESP32 - CAM: The ESP32-CAM has a very competitive small-size camera module that can operate independently as a minimum system with a footprint of only 27*40.5*4.5mm and a deep sleep current of up to 6mA.
  CP2102 USB UART: CP2102 USB UART FTDI
